// Digital circuit ALU_circuit.dig as structural Verilog
module ALU_circuit (
  input  [31:0] A,
  input  [31:0] B,
  input  [2:0] f3,
  input  sub,
  input  [6:0] opc,
  output [31:0] S
);

  wire and_2_out, and_3_out, and_4_out, multiplexer_7_out, or_2_out;
  wire [0:0] comparator_1_lt, comparator_2_lt;
  wire [2:0] multiplexer_1_out, multiplexer_2_out, multiplexer_3_out, multiplexer_4_out, multiplexer_5_out,
       MUX_alu;
  wire [31:0] add_1_s, and_1_out, barrelshifter_1_out, barrelshifter_2_out, barrelshifter_3_out,
       multiplexer_8_out, multiplexer_9_out, or_1_out, sub_1_s, xor_1_out;

  Multiplexer #(.Bits(3)) multiplexer_1 (.sel(f3[1]), .in_0(3'b010), .in_1(3'b011), .out(multiplexer_1_out));
  Multiplexer #(.Selector_Bits(2), .Bits(3)) multiplexer_2 (
    .sel({f3[2], f3[0]}), .in_0(3'b000), .in_1(3'b000), .in_2(multiplexer_1_out), .in_3(multiplexer_1_out),
    .out(multiplexer_2_out));
  Multiplexer #(.Bits(3)) multiplexer_3 (
    .sel(opc[6]), .in_0(3'b000), .in_1(multiplexer_2_out), .out(multiplexer_3_out));
  Multiplexer #(.Bits(3)) multiplexer_4 (
    .sel(opc[5]), .in_0(3'b000), .in_1(multiplexer_3_out), .out(multiplexer_4_out));
  Multiplexer #(.Bits(3)) multiplexer_5 (.sel(opc[4]), .in_0(multiplexer_4_out), .in_1(f3), .out(multiplexer_5_out));
  Multiplexer #(.Bits(3)) multiplexer_6 (.sel(opc[2]), .in_0(multiplexer_5_out), .in_1(3'b000), .out(MUX_alu));
  Add #(.Bits(32)) add_1 (.a(A), .b(B), .c_i(1'b0), .s(add_1_s));  // open: c_o
  Sub #(.Bits(32)) sub_1 (.a(A), .b(B), .c_i(1'b0), .s(sub_1_s));  // open: c_o
  BarrelShifter #(.Bits(32)) barrelshifter_1 (.in(A), .shift(B[5:0]), .out(barrelshifter_1_out));
  Comparator #(.Signed("true"), .Bits(32)) comparator_1 (.a(A), .b(B), .lt(comparator_1_lt[0]));  // open: gt, eq
  Comparator #(.Bits(32)) comparator_2 (.a(A), .b(B), .lt(comparator_2_lt[0]));  // open: gt, eq
  assign xor_1_out = A ^ B;  // XOr xor_1, 32 bits wide
  BarrelShifter #(.Bits(32), .direction("right")) barrelshifter_2 (.in(A), .shift(B[5:0]), .out(barrelshifter_2_out));
  BarrelShifter #(.Bits(32), .barrelShifterMode("arithmetic"), .barrelSigned("true"), .direction("right")) barrelshifter_3 (
    .in(A), .shift(B[6:0]), .out(barrelshifter_3_out));
  assign or_1_out = A | B;  // Or or_1, 32 bits wide
  assign and_1_out = A & B;  // And and_1, 32 bits wide
  and and_2 (and_2_out, ~f3[2], opc[6], opc[5], ~opc[4], ~opc[2]);  // And
  Multiplexer multiplexer_7 (.sel(or_2_out), .in_0(and_2_out), .in_1(sub), .out(multiplexer_7_out));
  Multiplexer #(.Bits(32)) multiplexer_8 (
    .sel(multiplexer_7_out), .in_0(add_1_s), .in_1(sub_1_s), .out(multiplexer_8_out));
  Multiplexer #(.Bits(32)) multiplexer_9 (
    .sel(multiplexer_7_out), .in_0(barrelshifter_2_out), .in_1(barrelshifter_3_out), .out(multiplexer_9_out));
  or or_2 (or_2_out, and_4_out, and_3_out);
  and and_3 (and_3_out, opc[5], opc[4], ~opc[2]);  // And
  and and_4 (and_4_out, f3[2], ~f3[1], f3[0], ~opc[5], opc[4], ~opc[2]);  // And
  Multiplexer #(.Selector_Bits(3), .Bits(32)) multiplexer_10 (
    .sel(MUX_alu), .in_0(multiplexer_8_out), .in_1(barrelshifter_1_out),
    .in_2({{31{1'b0}}, comparator_1_lt[0]}), .in_3({{31{1'b0}}, comparator_2_lt[0]}), .in_4(xor_1_out),
    .in_5(multiplexer_9_out), .in_6(or_1_out), .in_7(and_1_out), .out(S));

  // Other names for the same wires on the sheet: f3_0 = f3[0]; f3_1 = f3[1]; f3_2 = f3[2]; f7_2 = opc[2];
  //   f7_4 = opc[4]; f7_5 = opc[5]; f7_6 = opc[6]
endmodule
