// Digital circuit Banc_registres.dig as structural Verilog
module Banc_registres (
  input  Wreg,
  input  [4:0] Rd,
  input  [31:0] Data,
  input  [4:0] Rs1,
  input  [4:0] Rs2,
  input  [4:0] Rs3,
  output [31:0] Src1,
  output [31:0] Src2,
  output [31:0] TEST
);

  wire demultiplexer_1_out_0, demultiplexer_1_out_1, demultiplexer_2_out_0, demultiplexer_2_out_1,
       demultiplexer_3_out_0, demultiplexer_3_out_1, demultiplexer_4_out_0, demultiplexer_4_out_1,
       demultiplexer_5_out_0, demultiplexer_5_out_1, demultiplexer_6_out_0, demultiplexer_6_out_1,
       demultiplexer_7_out_0, demultiplexer_7_out_1, demultiplexer_8_out_0, demultiplexer_8_out_1,
       demultiplexer_9_out_0, demultiplexer_9_out_1, demultiplexer_10_out_0, demultiplexer_10_out_1,
       demultiplexer_11_out_0, demultiplexer_11_out_1, demultiplexer_12_out_0, demultiplexer_12_out_1,
       demultiplexer_13_out_0, demultiplexer_13_out_1, demultiplexer_14_out_0, demultiplexer_14_out_1,
       demultiplexer_15_out_0, demultiplexer_15_out_1, demultiplexer_16_out_0, demultiplexer_16_out_1,
       demultiplexer_17_out_0, demultiplexer_17_out_1, demultiplexer_18_out_0, demultiplexer_18_out_1,
       demultiplexer_19_out_0, demultiplexer_19_out_1, demultiplexer_20_out_0, demultiplexer_20_out_1,
       demultiplexer_21_out_0, demultiplexer_21_out_1, demultiplexer_22_out_0, demultiplexer_22_out_1,
       demultiplexer_23_out_0, demultiplexer_23_out_1, demultiplexer_24_out_0, demultiplexer_24_out_1,
       demultiplexer_25_out_0, demultiplexer_25_out_1, demultiplexer_26_out_0, demultiplexer_26_out_1,
       demultiplexer_27_out_0, demultiplexer_27_out_1, demultiplexer_28_out_0, demultiplexer_28_out_1,
       demultiplexer_29_out_0, demultiplexer_29_out_1, demultiplexer_30_out_0, demultiplexer_30_out_1,
       demultiplexer_31_out_0, demultiplexer_31_out_1;
  wire [31:0] multiplexer_1_out, multiplexer_2_out, multiplexer_3_out, multiplexer_4_out, multiplexer_5_out,
       multiplexer_6_out, multiplexer_7_out, multiplexer_8_out, multiplexer_9_out, multiplexer_10_out,
       multiplexer_11_out, multiplexer_12_out, multiplexer_13_out, multiplexer_14_out, multiplexer_15_out,
       multiplexer_16_out, multiplexer_17_out, multiplexer_18_out, multiplexer_19_out, multiplexer_20_out,
       multiplexer_21_out, multiplexer_22_out, multiplexer_23_out, multiplexer_24_out, multiplexer_25_out,
       multiplexer_26_out, multiplexer_27_out, multiplexer_28_out, multiplexer_29_out, multiplexer_30_out,
       multiplexer_31_out, multiplexer_32_out, multiplexer_33_out, multiplexer_34_out, multiplexer_35_out,
       multiplexer_36_out, multiplexer_37_out, multiplexer_38_out, multiplexer_39_out, multiplexer_40_out,
       multiplexer_41_out, multiplexer_42_out, multiplexer_43_out, multiplexer_44_out, multiplexer_46_out,
       multiplexer_47_out, multiplexer_48_out, multiplexer_49_out, multiplexer_50_out, multiplexer_51_out,
       multiplexer_52_out, multiplexer_53_out, multiplexer_54_out, multiplexer_55_out, multiplexer_56_out,
       multiplexer_57_out, multiplexer_58_out, multiplexer_59_out, multiplexer_61_out, multiplexer_62_out,
       x0_q, x1_q, x2_q, x3_q, x4_q, x5_q, x6_q, x7_q, x8_q, x9_q, x10_q, x11_q, x12_q, x13_q, x14_q, x15_q,
       x16_q, x17_q, x18_q, x19_q, x20_q, x21_q, x22_q, x23_q, x24_q, x25_q, x26_q, x27_q, x28_q, x29_q,
       x30_q, x31_q;

  Demultiplexer demultiplexer_1 (.sel(Rd[4]), .in(Wreg), .out_0(demultiplexer_1_out_0), .out_1(demultiplexer_1_out_1));
  Demultiplexer demultiplexer_2 (
    .sel(Rd[3]), .in(demultiplexer_1_out_0), .out_0(demultiplexer_2_out_0), .out_1(demultiplexer_2_out_1));
  Demultiplexer demultiplexer_3 (
    .sel(Rd[3]), .in(demultiplexer_1_out_1), .out_0(demultiplexer_3_out_0), .out_1(demultiplexer_3_out_1));
  Demultiplexer demultiplexer_4 (
    .sel(Rd[2]), .in(demultiplexer_2_out_0), .out_0(demultiplexer_4_out_0), .out_1(demultiplexer_4_out_1));
  Demultiplexer demultiplexer_5 (
    .sel(Rd[2]), .in(demultiplexer_2_out_1), .out_0(demultiplexer_5_out_0), .out_1(demultiplexer_5_out_1));
  Demultiplexer demultiplexer_6 (
    .sel(Rd[2]), .in(demultiplexer_3_out_0), .out_0(demultiplexer_6_out_0), .out_1(demultiplexer_6_out_1));
  Demultiplexer demultiplexer_7 (
    .sel(Rd[2]), .in(demultiplexer_3_out_1), .out_0(demultiplexer_7_out_0), .out_1(demultiplexer_7_out_1));
  Demultiplexer demultiplexer_8 (
    .sel(Rd[1]), .in(demultiplexer_4_out_0), .out_0(demultiplexer_8_out_0), .out_1(demultiplexer_8_out_1));
  Demultiplexer demultiplexer_9 (
    .sel(Rd[1]), .in(demultiplexer_4_out_1), .out_0(demultiplexer_9_out_0), .out_1(demultiplexer_9_out_1));
  Demultiplexer demultiplexer_10 (
    .sel(Rd[1]), .in(demultiplexer_5_out_0), .out_0(demultiplexer_10_out_0), .out_1(demultiplexer_10_out_1));
  Demultiplexer demultiplexer_11 (
    .sel(Rd[1]), .in(demultiplexer_5_out_1), .out_0(demultiplexer_11_out_0), .out_1(demultiplexer_11_out_1));
  Demultiplexer demultiplexer_12 (
    .sel(Rd[1]), .in(demultiplexer_6_out_0), .out_0(demultiplexer_12_out_0), .out_1(demultiplexer_12_out_1));
  Demultiplexer demultiplexer_13 (
    .sel(Rd[1]), .in(demultiplexer_6_out_1), .out_0(demultiplexer_13_out_0), .out_1(demultiplexer_13_out_1));
  Demultiplexer demultiplexer_14 (
    .sel(Rd[1]), .in(demultiplexer_7_out_0), .out_0(demultiplexer_14_out_0), .out_1(demultiplexer_14_out_1));
  Demultiplexer demultiplexer_15 (
    .sel(Rd[1]), .in(demultiplexer_7_out_1), .out_0(demultiplexer_15_out_0), .out_1(demultiplexer_15_out_1));
  Demultiplexer demultiplexer_16 (
    .sel(Rd[0]), .in(demultiplexer_8_out_0), .out_0(demultiplexer_16_out_0), .out_1(demultiplexer_16_out_1));
  Demultiplexer demultiplexer_17 (
    .sel(Rd[0]), .in(demultiplexer_8_out_1), .out_0(demultiplexer_17_out_0), .out_1(demultiplexer_17_out_1));
  Demultiplexer demultiplexer_18 (
    .sel(Rd[0]), .in(demultiplexer_9_out_0), .out_0(demultiplexer_18_out_0), .out_1(demultiplexer_18_out_1));
  Demultiplexer demultiplexer_19 (
    .sel(Rd[0]), .in(demultiplexer_9_out_1), .out_0(demultiplexer_19_out_0), .out_1(demultiplexer_19_out_1));
  Demultiplexer demultiplexer_20 (
    .sel(Rd[0]), .in(demultiplexer_10_out_0), .out_0(demultiplexer_20_out_0), .out_1(demultiplexer_20_out_1));
  Demultiplexer demultiplexer_21 (
    .sel(Rd[0]), .in(demultiplexer_10_out_1), .out_0(demultiplexer_21_out_0), .out_1(demultiplexer_21_out_1));
  Demultiplexer demultiplexer_22 (
    .sel(Rd[0]), .in(demultiplexer_11_out_0), .out_0(demultiplexer_22_out_0), .out_1(demultiplexer_22_out_1));
  Demultiplexer demultiplexer_23 (
    .sel(Rd[0]), .in(demultiplexer_11_out_1), .out_0(demultiplexer_23_out_0), .out_1(demultiplexer_23_out_1));
  Demultiplexer demultiplexer_24 (
    .sel(Rd[0]), .in(demultiplexer_12_out_0), .out_0(demultiplexer_24_out_0), .out_1(demultiplexer_24_out_1));
  Demultiplexer demultiplexer_25 (
    .sel(Rd[0]), .in(demultiplexer_12_out_1), .out_0(demultiplexer_25_out_0), .out_1(demultiplexer_25_out_1));
  Demultiplexer demultiplexer_26 (
    .sel(Rd[0]), .in(demultiplexer_13_out_0), .out_0(demultiplexer_26_out_0), .out_1(demultiplexer_26_out_1));
  Demultiplexer demultiplexer_27 (
    .sel(Rd[0]), .in(demultiplexer_13_out_1), .out_0(demultiplexer_27_out_0), .out_1(demultiplexer_27_out_1));
  Demultiplexer demultiplexer_28 (
    .sel(Rd[0]), .in(demultiplexer_14_out_0), .out_0(demultiplexer_28_out_0), .out_1(demultiplexer_28_out_1));
  Demultiplexer demultiplexer_29 (
    .sel(Rd[0]), .in(demultiplexer_14_out_1), .out_0(demultiplexer_29_out_0), .out_1(demultiplexer_29_out_1));
  Demultiplexer demultiplexer_30 (
    .sel(Rd[0]), .in(demultiplexer_15_out_0), .out_0(demultiplexer_30_out_0), .out_1(demultiplexer_30_out_1));
  Demultiplexer demultiplexer_31 (
    .sel(Rd[0]), .in(demultiplexer_15_out_1), .out_0(demultiplexer_31_out_0), .out_1(demultiplexer_31_out_1));
  D_FF #(.Bits(32)) x0 (.D({32{1'b0}}), .C(demultiplexer_16_out_0), .Q(x0_q));  // open: nQ
  D_FF #(.Bits(32)) x2 (.D(Data), .C(demultiplexer_17_out_0), .Q(x2_q));  // open: nQ
  D_FF #(.Bits(32)) x4 (.D(Data), .C(demultiplexer_18_out_0), .Q(x4_q));  // open: nQ
  D_FF #(.Bits(32)) x6 (.D(Data), .C(demultiplexer_19_out_0), .Q(x6_q));  // open: nQ
  D_FF #(.Bits(32)) x8 (.D(Data), .C(demultiplexer_20_out_0), .Q(x8_q));  // open: nQ
  D_FF #(.Bits(32)) x10 (.D(Data), .C(demultiplexer_21_out_0), .Q(x10_q));  // open: nQ
  D_FF #(.Bits(32)) x12 (.D(Data), .C(demultiplexer_22_out_0), .Q(x12_q));  // open: nQ
  D_FF #(.Bits(32)) x14 (.D(Data), .C(demultiplexer_23_out_0), .Q(x14_q));  // open: nQ
  D_FF #(.Bits(32)) x16 (.D(Data), .C(demultiplexer_24_out_0), .Q(x16_q));  // open: nQ
  D_FF #(.Bits(32)) x18 (.D(Data), .C(demultiplexer_25_out_0), .Q(x18_q));  // open: nQ
  D_FF #(.Bits(32)) x20 (.D(Data), .C(demultiplexer_26_out_0), .Q(x20_q));  // open: nQ
  D_FF #(.Bits(32)) x22 (.D(Data), .C(demultiplexer_27_out_0), .Q(x22_q));  // open: nQ
  D_FF #(.Bits(32)) x24 (.D(Data), .C(demultiplexer_28_out_0), .Q(x24_q));  // open: nQ
  D_FF #(.Bits(32)) x26 (.D(Data), .C(demultiplexer_29_out_0), .Q(x26_q));  // open: nQ
  D_FF #(.Bits(32)) x28 (.D(Data), .C(demultiplexer_30_out_0), .Q(x28_q));  // open: nQ
  D_FF #(.Bits(32)) x30 (.D(Data), .C(demultiplexer_31_out_0), .Q(x30_q));  // open: nQ
  D_FF #(.Bits(32)) x1 (.D(Data), .C(demultiplexer_16_out_1), .Q(x1_q));  // open: nQ
  D_FF #(.Bits(32)) x3 (.D(Data), .C(demultiplexer_17_out_1), .Q(x3_q));  // open: nQ
  D_FF #(.Bits(32)) x5 (.D(Data), .C(demultiplexer_18_out_1), .Q(x5_q));  // open: nQ
  D_FF #(.Bits(32)) x7 (.D(Data), .C(demultiplexer_19_out_1), .Q(x7_q));  // open: nQ
  D_FF #(.Bits(32)) x9 (.D(Data), .C(demultiplexer_20_out_1), .Q(x9_q));  // open: nQ
  D_FF #(.Bits(32)) x11 (.D(Data), .C(demultiplexer_21_out_1), .Q(x11_q));  // open: nQ
  D_FF #(.Bits(32)) x13 (.D(Data), .C(demultiplexer_22_out_1), .Q(x13_q));  // open: nQ
  D_FF #(.Bits(32)) x15 (.D(Data), .C(demultiplexer_23_out_1), .Q(x15_q));  // open: nQ
  D_FF #(.Bits(32)) x17 (.D(Data), .C(demultiplexer_24_out_1), .Q(x17_q));  // open: nQ
  D_FF #(.Bits(32)) x19 (.D(Data), .C(demultiplexer_25_out_1), .Q(x19_q));  // open: nQ
  D_FF #(.Bits(32)) x21 (.D(Data), .C(demultiplexer_26_out_1), .Q(x21_q));  // open: nQ
  D_FF #(.Bits(32)) x23 (.D(Data), .C(demultiplexer_27_out_1), .Q(x23_q));  // open: nQ
  D_FF #(.Bits(32)) x25 (.D(Data), .C(demultiplexer_28_out_1), .Q(x25_q));  // open: nQ
  D_FF #(.Bits(32)) x27 (.D(Data), .C(demultiplexer_29_out_1), .Q(x27_q));  // open: nQ
  D_FF #(.Bits(32)) x29 (.D(Data), .C(demultiplexer_30_out_1), .Q(x29_q));  // open: nQ
  D_FF #(.Bits(32)) x31 (.D(Data), .C(demultiplexer_31_out_1), .Q(x31_q));  // open: nQ
  Multiplexer #(.Bits(32)) multiplexer_1 (.sel(Rs1[0]), .in_0(x0_q), .in_1(x1_q), .out(multiplexer_1_out));
  Multiplexer #(.Bits(32)) multiplexer_2 (.sel(Rs1[0]), .in_0(x2_q), .in_1(x3_q), .out(multiplexer_2_out));
  Multiplexer #(.Bits(32)) multiplexer_3 (.sel(Rs1[0]), .in_0(x4_q), .in_1(x5_q), .out(multiplexer_3_out));
  Multiplexer #(.Bits(32)) multiplexer_4 (.sel(Rs1[0]), .in_0(x6_q), .in_1(x7_q), .out(multiplexer_4_out));
  Multiplexer #(.Bits(32)) multiplexer_5 (.sel(Rs1[0]), .in_0(x8_q), .in_1(x9_q), .out(multiplexer_5_out));
  Multiplexer #(.Bits(32)) multiplexer_6 (.sel(Rs1[0]), .in_0(x10_q), .in_1(x11_q), .out(multiplexer_6_out));
  Multiplexer #(.Bits(32)) multiplexer_7 (.sel(Rs1[0]), .in_0(x12_q), .in_1(x13_q), .out(multiplexer_7_out));
  Multiplexer #(.Bits(32)) multiplexer_8 (.sel(Rs1[0]), .in_0(x14_q), .in_1(x15_q), .out(multiplexer_8_out));
  Multiplexer #(.Bits(32)) multiplexer_9 (.sel(Rs1[0]), .in_0(x16_q), .in_1(x17_q), .out(multiplexer_9_out));
  Multiplexer #(.Bits(32)) multiplexer_10 (.sel(Rs1[0]), .in_0(x18_q), .in_1(x19_q), .out(multiplexer_10_out));
  Multiplexer #(.Bits(32)) multiplexer_11 (.sel(Rs1[0]), .in_0(x20_q), .in_1(x21_q), .out(multiplexer_11_out));
  Multiplexer #(.Bits(32)) multiplexer_12 (.sel(Rs1[0]), .in_0(x22_q), .in_1(x23_q), .out(multiplexer_12_out));
  Multiplexer #(.Bits(32)) multiplexer_13 (.sel(Rs1[0]), .in_0(x24_q), .in_1(x25_q), .out(multiplexer_13_out));
  Multiplexer #(.Bits(32)) multiplexer_14 (.sel(Rs1[0]), .in_0(x26_q), .in_1(x27_q), .out(multiplexer_14_out));
  Multiplexer #(.Bits(32)) multiplexer_15 (.sel(Rs1[0]), .in_0(x28_q), .in_1(x29_q), .out(multiplexer_15_out));
  Multiplexer #(.Bits(32)) multiplexer_16 (.sel(Rs1[0]), .in_0(x30_q), .in_1(x31_q), .out(multiplexer_16_out));
  Multiplexer #(.Bits(32)) multiplexer_17 (
    .sel(Rs1[1]), .in_0(multiplexer_1_out), .in_1(multiplexer_2_out), .out(multiplexer_17_out));
  Multiplexer #(.Bits(32)) multiplexer_18 (
    .sel(Rs1[1]), .in_0(multiplexer_3_out), .in_1(multiplexer_4_out), .out(multiplexer_18_out));
  Multiplexer #(.Bits(32)) multiplexer_19 (
    .sel(Rs1[1]), .in_0(multiplexer_5_out), .in_1(multiplexer_6_out), .out(multiplexer_19_out));
  Multiplexer #(.Bits(32)) multiplexer_20 (
    .sel(Rs1[1]), .in_0(multiplexer_7_out), .in_1(multiplexer_8_out), .out(multiplexer_20_out));
  Multiplexer #(.Bits(32)) multiplexer_21 (
    .sel(Rs1[1]), .in_0(multiplexer_9_out), .in_1(multiplexer_10_out), .out(multiplexer_21_out));
  Multiplexer #(.Bits(32)) multiplexer_22 (
    .sel(Rs1[1]), .in_0(multiplexer_11_out), .in_1(multiplexer_12_out), .out(multiplexer_22_out));
  Multiplexer #(.Bits(32)) multiplexer_23 (
    .sel(Rs1[1]), .in_0(multiplexer_13_out), .in_1(multiplexer_14_out), .out(multiplexer_23_out));
  Multiplexer #(.Bits(32)) multiplexer_24 (
    .sel(Rs1[1]), .in_0(multiplexer_15_out), .in_1(multiplexer_16_out), .out(multiplexer_24_out));
  Multiplexer #(.Bits(32)) multiplexer_25 (.sel(Rs2[0]), .in_0(x0_q), .in_1(x1_q), .out(multiplexer_25_out));
  Multiplexer #(.Bits(32)) multiplexer_26 (.sel(Rs2[0]), .in_0(x2_q), .in_1(x3_q), .out(multiplexer_26_out));
  Multiplexer #(.Bits(32)) multiplexer_27 (.sel(Rs2[0]), .in_0(x4_q), .in_1(x5_q), .out(multiplexer_27_out));
  Multiplexer #(.Bits(32)) multiplexer_28 (.sel(Rs2[0]), .in_0(x6_q), .in_1(x7_q), .out(multiplexer_28_out));
  Multiplexer #(.Bits(32)) multiplexer_29 (.sel(Rs2[0]), .in_0(x8_q), .in_1(x9_q), .out(multiplexer_29_out));
  Multiplexer #(.Bits(32)) multiplexer_30 (.sel(Rs2[0]), .in_0(x10_q), .in_1(x11_q), .out(multiplexer_30_out));
  Multiplexer #(.Bits(32)) multiplexer_31 (.sel(Rs2[0]), .in_0(x12_q), .in_1(x13_q), .out(multiplexer_31_out));
  Multiplexer #(.Bits(32)) multiplexer_32 (.sel(Rs2[0]), .in_0(x14_q), .in_1(x15_q), .out(multiplexer_32_out));
  Multiplexer #(.Bits(32)) multiplexer_33 (.sel(Rs2[0]), .in_0(x16_q), .in_1(x17_q), .out(multiplexer_33_out));
  Multiplexer #(.Bits(32)) multiplexer_34 (.sel(Rs2[0]), .in_0(x18_q), .in_1(x19_q), .out(multiplexer_34_out));
  Multiplexer #(.Bits(32)) multiplexer_35 (.sel(Rs2[0]), .in_0(x20_q), .in_1(x21_q), .out(multiplexer_35_out));
  Multiplexer #(.Bits(32)) multiplexer_36 (.sel(Rs2[0]), .in_0(x22_q), .in_1(x23_q), .out(multiplexer_36_out));
  Multiplexer #(.Bits(32)) multiplexer_37 (.sel(Rs2[0]), .in_0(x24_q), .in_1(x25_q), .out(multiplexer_37_out));
  Multiplexer #(.Bits(32)) multiplexer_38 (.sel(Rs2[0]), .in_0(x26_q), .in_1(x27_q), .out(multiplexer_38_out));
  Multiplexer #(.Bits(32)) multiplexer_39 (.sel(Rs2[0]), .in_0(x28_q), .in_1(x29_q), .out(multiplexer_39_out));
  Multiplexer #(.Bits(32)) multiplexer_40 (.sel(Rs2[0]), .in_0(x30_q), .in_1(x31_q), .out(multiplexer_40_out));
  Multiplexer #(.Bits(32)) multiplexer_41 (
    .sel(Rs1[2]), .in_0(multiplexer_17_out), .in_1(multiplexer_18_out), .out(multiplexer_41_out));
  Multiplexer #(.Bits(32)) multiplexer_42 (
    .sel(Rs1[2]), .in_0(multiplexer_19_out), .in_1(multiplexer_20_out), .out(multiplexer_42_out));
  Multiplexer #(.Bits(32)) multiplexer_43 (
    .sel(Rs1[2]), .in_0(multiplexer_21_out), .in_1(multiplexer_22_out), .out(multiplexer_43_out));
  Multiplexer #(.Bits(32)) multiplexer_44 (
    .sel(Rs1[2]), .in_0(multiplexer_23_out), .in_1(multiplexer_24_out), .out(multiplexer_44_out));
  Multiplexer #(.Selector_Bits(5), .Bits(32)) multiplexer_45 (
    .sel(Rs3), .in_0(x0_q), .in_1(x1_q), .in_2(x2_q), .in_3(x3_q), .in_4(x4_q), .in_5(x5_q), .in_6(x6_q),
    .in_7(x7_q), .in_8(x8_q), .in_9(x9_q), .in_10(x10_q), .in_11(x11_q), .in_12(x12_q), .in_13(x13_q),
    .in_14(x14_q), .in_15(x15_q), .in_16(x16_q), .in_17(x17_q), .in_18(x18_q), .in_19(x19_q), .in_20(x20_q),
    .in_21(x21_q), .in_22(x22_q), .in_23(x23_q), .in_24(x24_q), .in_25(x25_q), .in_26(x26_q), .in_27(x27_q),
    .in_28(x28_q), .in_29(x29_q), .in_30(x30_q), .in_31(x31_q), .out(TEST));
  Multiplexer #(.Bits(32)) multiplexer_46 (
    .sel(Rs2[1]), .in_0(multiplexer_25_out), .in_1(multiplexer_26_out), .out(multiplexer_46_out));
  Multiplexer #(.Bits(32)) multiplexer_47 (
    .sel(Rs2[1]), .in_0(multiplexer_27_out), .in_1(multiplexer_28_out), .out(multiplexer_47_out));
  Multiplexer #(.Bits(32)) multiplexer_48 (
    .sel(Rs2[1]), .in_0(multiplexer_29_out), .in_1(multiplexer_30_out), .out(multiplexer_48_out));
  Multiplexer #(.Bits(32)) multiplexer_49 (
    .sel(Rs2[1]), .in_0(multiplexer_31_out), .in_1(multiplexer_32_out), .out(multiplexer_49_out));
  Multiplexer #(.Bits(32)) multiplexer_50 (
    .sel(Rs2[1]), .in_0(multiplexer_33_out), .in_1(multiplexer_34_out), .out(multiplexer_50_out));
  Multiplexer #(.Bits(32)) multiplexer_51 (
    .sel(Rs2[1]), .in_0(multiplexer_35_out), .in_1(multiplexer_36_out), .out(multiplexer_51_out));
  Multiplexer #(.Bits(32)) multiplexer_52 (
    .sel(Rs2[1]), .in_0(multiplexer_37_out), .in_1(multiplexer_38_out), .out(multiplexer_52_out));
  Multiplexer #(.Bits(32)) multiplexer_53 (
    .sel(Rs2[1]), .in_0(multiplexer_39_out), .in_1(multiplexer_40_out), .out(multiplexer_53_out));
  Multiplexer #(.Bits(32)) multiplexer_54 (
    .sel(Rs1[3]), .in_0(multiplexer_41_out), .in_1(multiplexer_42_out), .out(multiplexer_54_out));
  Multiplexer #(.Bits(32)) multiplexer_55 (
    .sel(Rs1[3]), .in_0(multiplexer_43_out), .in_1(multiplexer_44_out), .out(multiplexer_55_out));
  Multiplexer #(.Bits(32)) multiplexer_56 (
    .sel(Rs2[2]), .in_0(multiplexer_46_out), .in_1(multiplexer_47_out), .out(multiplexer_56_out));
  Multiplexer #(.Bits(32)) multiplexer_57 (
    .sel(Rs2[2]), .in_0(multiplexer_48_out), .in_1(multiplexer_49_out), .out(multiplexer_57_out));
  Multiplexer #(.Bits(32)) multiplexer_58 (
    .sel(Rs2[2]), .in_0(multiplexer_50_out), .in_1(multiplexer_51_out), .out(multiplexer_58_out));
  Multiplexer #(.Bits(32)) multiplexer_59 (
    .sel(Rs2[2]), .in_0(multiplexer_52_out), .in_1(multiplexer_53_out), .out(multiplexer_59_out));
  Multiplexer #(.Bits(32)) multiplexer_60 (
    .sel(Rs1[4]), .in_0(multiplexer_54_out), .in_1(multiplexer_55_out), .out(Src1));
  Multiplexer #(.Bits(32)) multiplexer_61 (
    .sel(Rs2[3]), .in_0(multiplexer_56_out), .in_1(multiplexer_57_out), .out(multiplexer_61_out));
  Multiplexer #(.Bits(32)) multiplexer_62 (
    .sel(Rs2[3]), .in_0(multiplexer_58_out), .in_1(multiplexer_59_out), .out(multiplexer_62_out));
  Multiplexer #(.Bits(32)) multiplexer_63 (
    .sel(Rs2[4]), .in_0(multiplexer_61_out), .in_1(multiplexer_62_out), .out(Src2));
endmodule
