// Digital circuit Branch_manager.dig as structural Verilog
module Branch_manager (
  input  [31:0] Res,
  input  [2:0] f3,
  output Taken
);

  wire not_1_out, not_2_out, not_3_out, or_1_out;

  or or_1 (or_1_out, Res[0], Res[1], Res[2], Res[3], Res[4], Res[5], Res[6], Res[7], Res[8], Res[9], Res[10], Res[11], Res[12], Res[13], Res[14], Res[15], Res[16], Res[17], Res[18], Res[19], Res[20], Res[21], Res[22], Res[23], Res[24], Res[25], Res[26], Res[27], Res[28], Res[29], Res[30], Res[31]);
  not not_1 (not_1_out, or_1_out);
  not not_2 (not_2_out, Res[0]);
  not not_3 (not_3_out, Res[0]);
  Multiplexer #(.Selector_Bits(3)) multiplexer_1 (
    .sel(f3), .in_0(not_1_out), .in_1(or_1_out), .in_2(1'b0), .in_3(1'b0), .in_4(Res[0]), .in_5(not_2_out),
    .in_6(Res[0]), .in_7(not_3_out), .out(Taken));
endmodule
