// Digital circuit CC_flush.dig as structural Verilog
module CC_flush (
  input  Taken,
  input  C,
  output Flush
);

  wire and_1_out, not_1_out, not_2_out, Z_0_n, Z_1_n;

  not not_1 (not_1_out, Z_1_n);
  not not_2 (not_2_out, Z_0_n);
  and and_1 (and_1_out, Taken, not_2_out, not_1_out);
  or or_1 (Flush, Z_0_n, Z_1_n);
  D_FF u_Z_1_n (.D(Z_0_n), .C(C), .Q(Z_1_n));  // open: nQ
  D_FF u_Z_0_n (.D(and_1_out), .C(C), .Q(Z_0_n));  // open: nQ
  // Probe CC_flush.fsm on {Taken, Z_1_n, Z_0_n}

  // Notes on the sheet:
  //   C: Hz: 2
endmodule
