// Digital circuit CC_lpg.dig as structural Verilog
module CC_lpg (
  input  W_lpg,
  input  C,
  output Count,
  output WE,
  output en
);

  wire and_1_out, and_2_out, and_5_out, and_6_out, not_1_out, not_2_out, not_3_out, or_1_out, or_2_out,
       Z_0_n, Z_1_n;

  not not_1 (not_1_out, W_lpg);
  not not_2 (not_2_out, Z_1_n);
  not not_3 (not_3_out, Z_0_n);
  and and_1 (and_1_out, not_1_out, Z_1_n);
  and and_2 (and_2_out, W_lpg, not_3_out);
  and and_3 (WE, Z_0_n, not_2_out);
  and and_4 (Count, not_3_out, Z_1_n);
  and and_5 (and_5_out, Z_0_n, not_2_out);
  and and_6 (and_6_out, not_3_out, Z_1_n);
  or or_1 (or_1_out, and_1_out, Z_0_n);
  or or_2 (or_2_out, and_2_out, Z_1_n);
  or or_3 (en, and_5_out, and_6_out);
  D_FF u_Z_1_n (.D(or_1_out), .C(C), .Q(Z_1_n));  // open: nQ
  D_FF u_Z_0_n (.D(or_2_out), .C(C), .Q(Z_0_n));  // open: nQ
  // Probe CC_lpg.fsm on {W_lpg, Z_1_n, Z_0_n}

  // Notes on the sheet:
  //   C: Hz: 2
endmodule
