// Digital circuit CPU_pip_v2.dig as structural Verilog
module CPU_pip_v2 (
  input  [4:0] in_1,
  input  W,
  input  W_lpg,
  input  clk,
  input  clk_2,
  output [31:0] out_2
);

  wire and_1_out, and_2_out, and_3_out, and_4_out, Br_q, branch_manager_1_taken, cc_lpg_1_count, cc_lpg_1_en,
       cc_lpg_1_we, EXE_W, Flush, freeze_unit_1_freeze, IMM_sel_q, Jal_r_2_q, Jal_r_q, MEM_W,
       multiplexer_7_out, multiplexer_8_out, multiplexer_9_out, multiplexer_10_out, not_1_out, not_2_out,
       opc_dec_1_br, opc_dec_1_i, opc_dec_1_jal_r, opc_dec_1_ret, or_1_out, or_2_out, Ret_q, Taken, W_reg_3_q;
  wire [1:0] DMEM_sel_2_q, DMEM_sel_q, multiplexer_6_out, opc_dec_1_store;
  wire [4:0] EXE_Rd, MEM_Rd, multiplexer_3_out, Rd_3_q;
  wire [5:0] counter_1_out, multiplexer_2_out;
  wire [6:0] ALU_sel_q;
  wire [10:0] RI_q;
  wire [10:7] ALU_sel_q_2;
  wire [31:0] add_1_s, add_2_s, add_3_s, ALU_s, driver_2_out, IMEM_d, imm_dec_1_imm, IMM_q,
       multiplexer_1_out, multiplexer_4_out, multiplexer_5_out, multiplexer_11_out, multiplexer_12_out,
       multiplexer_13_out, multiplexer_14_out, PC_2_q, PC_3_q, PC_4_q, PC_q, reg_file_rv32i_1_src1,
       reg_file_rv32i_1_src2, Res_2_q, Res_q, rom_1_d, Src1_q, Src2_2_q, Src2_q;
  wire [31:7] RI_q_2;

  Add #(.Bits(32)) add_1 (.a(PC_q), .b(32'h4), .c_i(1'b0), .s(add_1_s));  // open: c_o
  Multiplexer #(.Bits(32)) multiplexer_1 (.sel(Taken), .in_0(add_1_s), .in_1(add_2_s), .out(multiplexer_1_out));
  Register #(.Bits(32)) PC (.D(multiplexer_1_out), .C(and_2_out), .en(not_1_out), .Q(PC_q));
  CC_lpg cc_lpg_1 (.WE(cc_lpg_1_we), .Count(cc_lpg_1_count), .en(cc_lpg_1_en), .C(clk), .W_lpg(W_lpg));
  Counter #(.Bits(6)) counter_1 (.en(1'b1), .C(cc_lpg_1_count), .clr(1'b0), .out(counter_1_out));  // open: ovf
  Multiplexer #(.Bits(6)) multiplexer_2 (
    .sel(cc_lpg_1_en), .in_0(PC_q[7:2]), .in_1(counter_1_out), .out(multiplexer_2_out));
  and and_1 (and_1_out, cc_lpg_1_en, cc_lpg_1_we);
  ROM #(.AddrBits(6), .Bits(32)) rom_1 (.A(counter_1_out), .sel(1'b1), .D(rom_1_d));
  RAMSinglePortSel #(.AddrBits(6), .Bits(32)) IMEM (
    .A(multiplexer_2_out), .CS(1'b1), .WE(and_1_out), .OE(~cc_lpg_1_en), .D(IMEM_d));
  assign IMEM_d = cc_lpg_1_en ? rom_1_d : 32'bz;  // Driver driver_1
  Register #(.Bits(32)) RI (
    .D(IMEM_d), .C(and_2_out), .en(not_1_out),
    .Q({RI_q_2[31], RI_q[10], RI_q_2[29:15], RI_q[9:7], RI_q_2[11:7], RI_q[6:0]}));
  Register #(.Bits(32)) PC_2 (.D(PC_q), .C(and_2_out), .en(not_1_out), .Q(PC_2_q));
  and and_2 (and_2_out, W, clk_2);
  OPC_dec opc_dec_1 (
    .opc(RI_q[6:0]), .I(opc_dec_1_i), .Br(opc_dec_1_br), .Jal_r(opc_dec_1_jal_r), .Ret(opc_dec_1_ret),
    .Store(opc_dec_1_store[0]), .Load(opc_dec_1_store[1]));  // open: R, Lui, Auipc
  Freeze_Unit freeze_unit_1 (
    .Rs1(RI_q_2[19:15]), .Rs2(RI_q_2[24:20]), .EXE_Wreg(EXE_W), .EXE_Rd(EXE_Rd), .MEM_Wreg(MEM_W),
    .MEM_Rd(MEM_Rd), .Freeze(freeze_unit_1_freeze));
  IMM_dec imm_dec_1 (
    .Ri({RI_q_2[31], RI_q[10], RI_q_2[29:15], RI_q[9:7], RI_q_2[11:7], RI_q[6:0]}),
    .Store(opc_dec_1_store[0]), .Jal_r(opc_dec_1_jal_r), .Ret(opc_dec_1_ret), .Br(opc_dec_1_br),
    .Imm(imm_dec_1_imm));
  Reg_file_rv32i reg_file_rv32i_1 (
    .Data(Res_2_q), .W_reg(W_reg_3_q), .Rd(Rd_3_q), .Rs1(RI_q_2[19:15]), .Rs2(RI_q_2[24:20]), .Rs3(in_1),
    .TEST(out_2), .Src1(reg_file_rv32i_1_src1), .Src2(reg_file_rv32i_1_src2));
  not not_1 (not_1_out, freeze_unit_1_freeze);
  LED led_1 (.in(freeze_unit_1_freeze));
  and and_3 (and_3_out, RI_q[0], RI_q[1], ~opc_dec_1_store[0], ~opc_dec_1_br);  // And
  or or_1 (or_1_out, opc_dec_1_i, opc_dec_1_store[0], opc_dec_1_store[1]);
  not not_2 (not_2_out, and_2_out);
  or or_2 (or_2_out, freeze_unit_1_freeze, Flush);
  CC_flush cc_flush_1 (.Taken(Taken), .C(not_2_out), .Flush(Flush));
  Multiplexer #(.Bits(5)) multiplexer_3 (
    .sel(or_2_out), .in_0(RI_q_2[11:7]), .in_1({5{1'b0}}), .out(multiplexer_3_out));
  Multiplexer #(.Bits(32)) multiplexer_4 (
    .sel(or_2_out), .in_0(reg_file_rv32i_1_src1), .in_1({32{1'b0}}), .out(multiplexer_4_out));
  Multiplexer #(.Bits(32)) multiplexer_5 (
    .sel(or_2_out), .in_0(reg_file_rv32i_1_src2), .in_1({32{1'b0}}), .out(multiplexer_5_out));
  Multiplexer #(.Bits(2)) multiplexer_6 (.sel(or_2_out), .in_0(opc_dec_1_store), .in_1(2'b00), .out(multiplexer_6_out));
  Multiplexer multiplexer_7 (.sel(or_2_out), .in_0(and_3_out), .in_1(1'b0), .out(multiplexer_7_out));
  Multiplexer multiplexer_8 (.sel(or_2_out), .in_0(opc_dec_1_br), .in_1(1'b0), .out(multiplexer_8_out));
  Multiplexer multiplexer_9 (.sel(or_2_out), .in_0(opc_dec_1_ret), .in_1(1'b0), .out(multiplexer_9_out));
  Multiplexer multiplexer_10 (.sel(or_2_out), .in_0(opc_dec_1_jal_r), .in_1(1'b0), .out(multiplexer_10_out));
  LED led_2 (.in(Flush));
  D_FF #(.Bits(5)) Rd (.D(multiplexer_3_out), .C(and_2_out), .Q(EXE_Rd));  // open: nQ
  D_FF #(.Bits(32)) Src1 (.D(multiplexer_4_out), .C(and_2_out), .Q(Src1_q));  // open: nQ
  D_FF #(.Bits(32)) Src2 (.D(multiplexer_5_out), .C(and_2_out), .Q(Src2_q));  // open: nQ
  D_FF #(.Bits(32)) PC_3 (.D(PC_2_q), .C(and_2_out), .Q(PC_3_q));  // open: nQ
  D_FF #(.Bits(32)) IMM (.D(imm_dec_1_imm), .C(and_2_out), .Q(IMM_q));  // open: nQ
  D_FF #(.Bits(11)) ALU_sel (.D(RI_q), .C(and_2_out), .Q({ALU_sel_q_2, ALU_sel_q}));  // open: nQ
  D_FF #(.Bits(2)) DMEM_sel (.D(multiplexer_6_out), .C(and_2_out), .Q(DMEM_sel_q));  // open: nQ
  D_FF W_reg (.D(multiplexer_7_out), .C(and_2_out), .Q(EXE_W));  // open: nQ
  D_FF Br (.D(multiplexer_8_out), .C(and_2_out), .Q(Br_q));  // open: nQ
  D_FF IMM_sel (.D(or_1_out), .C(and_2_out), .Q(IMM_sel_q));  // open: nQ
  D_FF Ret (.D(multiplexer_9_out), .C(and_2_out), .Q(Ret_q));  // open: nQ
  D_FF Jal_r (.D(multiplexer_10_out), .C(and_2_out), .Q(Jal_r_q));  // open: nQ
  Multiplexer #(.Bits(32)) multiplexer_11 (.sel(Ret_q), .in_0(PC_3_q), .in_1(Src1_q), .out(multiplexer_11_out));
  Add #(.Bits(32)) add_2 (.a(IMM_q), .b(multiplexer_11_out), .c_i(1'b0), .s(add_2_s));  // open: c_o
  Multiplexer #(.Bits(32)) multiplexer_12 (.sel(IMM_sel_q), .in_0(Src2_q), .in_1(IMM_q), .out(multiplexer_12_out));
  ALU_circuit ALU (
    .A(Src1_q), .B(multiplexer_12_out), .opc(ALU_sel_q), .f3(ALU_sel_q_2[9:7]), .sub(ALU_sel_q_2[10]),
    .S(ALU_s));
  Branch_manager branch_manager_1 (.Res(ALU_s), .f3(ALU_sel_q_2[9:7]), .Taken(branch_manager_1_taken));
  and and_4 (and_4_out, branch_manager_1_taken, Br_q);
  or or_3 (Taken, and_4_out, Jal_r_q);
  D_FF #(.Bits(5)) Rd_2 (.D(EXE_Rd), .C(and_2_out), .Q(MEM_Rd));  // open: nQ
  D_FF #(.Bits(32)) Res (.D(ALU_s), .C(and_2_out), .Q(Res_q));  // open: nQ
  D_FF #(.Bits(32)) Src2_2 (.D(Src2_q), .C(and_2_out), .Q(Src2_2_q));  // open: nQ
  D_FF #(.Bits(32)) PC_4 (.D(PC_3_q), .C(and_2_out), .Q(PC_4_q));  // open: nQ
  D_FF #(.Bits(2)) DMEM_sel_2 (.D(DMEM_sel_q), .C(and_2_out), .Q(DMEM_sel_2_q));  // open: nQ
  D_FF W_reg_2 (.D(EXE_W), .C(and_2_out), .Q(MEM_W));  // open: nQ
  D_FF Jal_r_2 (.D(Jal_r_q), .C(and_2_out), .Q(Jal_r_2_q));  // open: nQ
  assign driver_2_out = DMEM_sel_2_q[0] ? Src2_2_q : 32'bz;  // Driver driver_2
  RAMSinglePortSel #(.AddrBits(6), .Bits(32)) DMEM (
    .A(Res_q[7:2]), .CS(1'b1), .WE(DMEM_sel_2_q[0]), .OE(~DMEM_sel_2_q[0]), .D(driver_2_out));
  Add #(.Bits(32)) add_3 (.a(32'h4), .b(PC_4_q), .c_i(1'b0), .s(add_3_s));  // open: c_o
  Multiplexer #(.Bits(32)) multiplexer_13 (
    .sel(DMEM_sel_2_q[1]), .in_0(Res_q), .in_1(driver_2_out), .out(multiplexer_13_out));
  Multiplexer #(.Bits(32)) multiplexer_14 (
    .sel(Jal_r_2_q), .in_0(multiplexer_13_out), .in_1(add_3_s), .out(multiplexer_14_out));
  D_FF #(.Bits(5)) Rd_3 (.D(MEM_Rd), .C(and_2_out), .Q(Rd_3_q));  // open: nQ
  D_FF #(.Bits(32)) Res_2 (.D(multiplexer_14_out), .C(and_2_out), .Q(Res_2_q));  // open: nQ
  D_FF W_reg_3 (.D(MEM_W), .C(and_2_out), .Q(W_reg_3_q));  // open: nQ

  // Notes on the sheet:
  //   clk: Hz: 10
  //   clk_2: Hz: 2
  //   Load Program RV32i
  //   IF
  //   contents of rom_1 (hex, n*v repeats v):
  //   500093,a00113,2081b3,302023,2203,320463,100293,80036f,2a00393
  //   ,6300413,404e7
  //   IF/ID
  //   Freeze Unit
  //   WB
  //   ID
  //   Flush Unit
  //   ID/EXE
  //   EXE
  //   EXE/MEM
  //   MEM
  //   MEM/WB
endmodule
