// Digital circuit Freeze_Unit.dig as structural Verilog
module Freeze_Unit (
  input  [4:0] Rs1,
  input  [4:0] Rs2,
  input  [4:0] EXE_Rd,
  input  [4:0] MEM_Rd,
  input  MEM_Wreg,
  input  EXE_Wreg,
  output Freeze
);

  wire and_1_out, and_2_out, and_3_out, and_4_out, comparator_1_eq, comparator_2_eq, comparator_3_eq,
       comparator_4_eq, comparator_5_eq, comparator_6_eq;

  Comparator #(.Bits(5)) comparator_1 (.a(EXE_Rd), .b(Rs1), .eq(comparator_1_eq));  // open: gt, lt
  Comparator #(.Bits(5)) comparator_2 (.a(EXE_Rd), .b({5{1'b0}}), .eq(comparator_2_eq));  // open: gt, lt
  Comparator #(.Bits(5)) comparator_3 (.a(MEM_Rd), .b(Rs1), .eq(comparator_3_eq));  // open: gt, lt
  Comparator #(.Bits(5)) comparator_4 (.a(MEM_Rd), .b({5{1'b0}}), .eq(comparator_4_eq));  // open: gt, lt
  Comparator #(.Bits(5)) comparator_5 (.a(EXE_Rd), .b(Rs2), .eq(comparator_5_eq));  // open: gt, lt
  Comparator #(.Bits(5)) comparator_6 (.a(MEM_Rd), .b(Rs2), .eq(comparator_6_eq));  // open: gt, lt
  and and_1 (and_1_out, MEM_Wreg, comparator_3_eq, ~comparator_4_eq);  // And
  and and_2 (and_2_out, ~comparator_2_eq, EXE_Wreg, comparator_5_eq);  // And
  and and_3 (and_3_out, ~comparator_4_eq, MEM_Wreg, comparator_6_eq);  // And
  and and_4 (and_4_out, EXE_Wreg, comparator_1_eq, ~comparator_2_eq);  // And
  or or_1 (Freeze, and_4_out, and_1_out, and_2_out, and_3_out);
endmodule
