// Digital circuit IMM_dec.dig as structural Verilog
module IMM_dec (
  input  [31:0] Ri,
  input  Store,
  input  Br,
  input  Jal_r,
  input  Ret,
  output [31:0] Imm
);

  wire [1:1] and_1_out;
  wire [11:0] multiplexer_1_out;
  wire [31:0] bitextender_1_out, bitextender_2_out, bitextender_3_out;

  Multiplexer #(.Bits(12)) multiplexer_1 (
    .sel(Store), .in_0(Ri[31:20]), .in_1({Ri[31:25], Ri[11:7]}), .out(multiplexer_1_out));
  BitExtender #(.inputBits(12), .outputBits(32)) bitextender_1 (.in(multiplexer_1_out), .out(bitextender_1_out));
  BitExtender #(.inputBits(13), .outputBits(32)) bitextender_2 (
    .in({Ri[31], Ri[7], Ri[30:25], Ri[11:8], 1'b0}), .out(bitextender_2_out));
  BitExtender #(.inputBits(21), .outputBits(32)) bitextender_3 (
    .in({Ri[31], Ri[19:12], Ri[20], Ri[30:21], 1'b0}), .out(bitextender_3_out));
  and and_1 (and_1_out[1], Jal_r, ~Ret);  // And
  Multiplexer #(.Selector_Bits(2), .Bits(32)) multiplexer_2 (
    .sel({and_1_out[1], Br}), .in_0(bitextender_1_out), .in_1(bitextender_2_out), .in_2(bitextender_3_out),
    .in_3({32{1'b0}}), .out(Imm));

  // Notes on the sheet:
  //   store ou pas
endmodule
