// Digital circuit OPC_dec.dig as structural Verilog
module OPC_dec (
  input  [6:0] opc,
  output I,
  output R,
  output Br,
  output Jal_r,
  output Ret,
  output Lui,
  output Auipc,
  output Store,
  output Load
);

  wire and_1_out, and_2_out, and_3_out, and_4_out, and_5_out, and_6_out, and_7_out, and_8_out, and_9_out,
       and_10_out, and_11_out, and_12_out, and_13_out, and_14_out;

  and and_1 (and_1_out, ~opc[2], ~opc[3], opc[4], ~opc[6]);  // And
  and and_2 (and_2_out, ~opc[2], ~opc[3], ~opc[4], opc[5], opc[6]);  // And
  and and_3 (and_3_out, opc[2], ~opc[4], opc[5], opc[6]);  // And
  and and_4 (and_4_out, opc[2], ~opc[3], opc[4], ~opc[6]);  // And
  and and_5 (and_5_out, ~opc[2], ~opc[3], ~opc[4], ~opc[6]);  // And
  and and_6 (and_6_out, ~opc[2], ~opc[3], ~opc[4], ~opc[6]);  // And
  and and_7 (and_7_out, and_3_out, ~opc[3]);  // And
  and and_8 (and_8_out, opc[0], opc[1]);
  and and_9 (and_9_out, opc[5], and_1_out);
  and and_10 (and_10_out, and_1_out, ~opc[5]);  // And
  and and_11 (and_11_out, opc[5], and_4_out);
  and and_12 (and_12_out, and_4_out, ~opc[5]);  // And
  and and_13 (and_13_out, and_5_out, opc[5]);
  and and_14 (and_14_out, ~opc[5], and_6_out);  // And
  and and_15 (R, and_8_out, and_9_out);
  and and_16 (I, and_8_out, and_10_out);
  and and_17 (Br, and_8_out, and_2_out);
  and and_18 (Jal_r, and_8_out, and_3_out);
  and and_19 (Ret, and_8_out, and_7_out);
  and and_20 (Lui, and_8_out, and_11_out);
  and and_21 (Auipc, and_8_out, and_12_out);
  and and_22 (Store, and_8_out, and_13_out);
  and and_23 (Load, and_8_out, and_14_out);
endmodule
