// Digital circuit Reg_file_8x32_0.dig as structural Verilog
module Reg_file_8x32_0 (
  input  [2:0] Rd,
  input  [31:0] Data,
  input  W_reg,
  input  [2:0] Rs1,
  input  [2:0] Rs2,
  input  [2:0] Rs3,
  output [31:0] Src1,
  output [31:0] Src2,
  output [31:0] Src3
);

  wire and_1_out, and_2_out, and_3_out, and_4_out, and_5_out, and_6_out, and_7_out, and_8_out,
       decoder_1_out_0, decoder_1_out_1, decoder_1_out_2, decoder_1_out_3, decoder_1_out_4, decoder_1_out_5,
       decoder_1_out_6, decoder_1_out_7, decoder_2_out_0, decoder_2_out_1, decoder_2_out_2, decoder_2_out_3,
       decoder_2_out_4, decoder_2_out_5, decoder_2_out_6, decoder_2_out_7, decoder_3_out_0, decoder_3_out_1,
       decoder_3_out_2, decoder_3_out_3, decoder_3_out_4, decoder_3_out_5, decoder_3_out_6, decoder_3_out_7,
       decoder_4_out_0, decoder_4_out_1, decoder_4_out_2, decoder_4_out_3, decoder_4_out_4, decoder_4_out_5,
       decoder_4_out_6, decoder_4_out_7;
  wire [31:0] x0_q, x1_q, x2_q, x3_q, x4_q, x5_q, x6_q, x7_q;

  Decoder #(.Selector_Bits(3)) decoder_1 (
    .sel(Rd), .out_0(decoder_1_out_0), .out_1(decoder_1_out_1), .out_2(decoder_1_out_2),
    .out_3(decoder_1_out_3), .out_4(decoder_1_out_4), .out_5(decoder_1_out_5), .out_6(decoder_1_out_6),
    .out_7(decoder_1_out_7));
  and and_1 (and_1_out, W_reg, decoder_1_out_0);
  and and_2 (and_2_out, W_reg, decoder_1_out_1);
  and and_3 (and_3_out, W_reg, decoder_1_out_2);
  and and_4 (and_4_out, W_reg, decoder_1_out_3);
  and and_5 (and_5_out, W_reg, decoder_1_out_4);
  and and_6 (and_6_out, W_reg, decoder_1_out_5);
  and and_7 (and_7_out, W_reg, decoder_1_out_6);
  and and_8 (and_8_out, W_reg, decoder_1_out_7);
  D_FF #(.Bits(32)) x0 (.D({32{1'b0}}), .C(and_1_out), .Q(x0_q));  // open: nQ
  D_FF #(.Bits(32)) x1 (.D(Data), .C(and_2_out), .Q(x1_q));  // open: nQ
  D_FF #(.Bits(32)) x2 (.D(Data), .C(and_3_out), .Q(x2_q));  // open: nQ
  D_FF #(.Bits(32)) x3 (.D(Data), .C(and_4_out), .Q(x3_q));  // open: nQ
  D_FF #(.Bits(32)) x4 (.D(Data), .C(and_5_out), .Q(x4_q));  // open: nQ
  D_FF #(.Bits(32)) x5 (.D(Data), .C(and_6_out), .Q(x5_q));  // open: nQ
  D_FF #(.Bits(32)) x6 (.D(Data), .C(and_7_out), .Q(x6_q));  // open: nQ
  D_FF #(.Bits(32)) x7 (.D(Data), .C(and_8_out), .Q(x7_q));  // open: nQ
  assign Src1 = decoder_2_out_0 ? x0_q : 32'bz;  // Driver driver_1
  Decoder #(.Selector_Bits(3)) decoder_2 (
    .sel(Rs1), .out_0(decoder_2_out_0), .out_1(decoder_2_out_1), .out_2(decoder_2_out_2),
    .out_3(decoder_2_out_3), .out_4(decoder_2_out_4), .out_5(decoder_2_out_5), .out_6(decoder_2_out_6),
    .out_7(decoder_2_out_7));
  assign Src1 = decoder_2_out_1 ? x1_q : 32'bz;  // Driver driver_2
  assign Src1 = decoder_2_out_2 ? x2_q : 32'bz;  // Driver driver_3
  assign Src1 = decoder_2_out_3 ? x3_q : 32'bz;  // Driver driver_4
  assign Src1 = decoder_2_out_4 ? x4_q : 32'bz;  // Driver driver_5
  assign Src1 = decoder_2_out_5 ? x5_q : 32'bz;  // Driver driver_6
  assign Src1 = decoder_2_out_6 ? x6_q : 32'bz;  // Driver driver_7
  assign Src1 = decoder_2_out_7 ? x7_q : 32'bz;  // Driver driver_8
  assign Src2 = decoder_3_out_0 ? x0_q : 32'bz;  // Driver driver_9
  Decoder #(.Selector_Bits(3)) decoder_3 (
    .sel(Rs2), .out_0(decoder_3_out_0), .out_1(decoder_3_out_1), .out_2(decoder_3_out_2),
    .out_3(decoder_3_out_3), .out_4(decoder_3_out_4), .out_5(decoder_3_out_5), .out_6(decoder_3_out_6),
    .out_7(decoder_3_out_7));
  assign Src2 = decoder_3_out_1 ? x1_q : 32'bz;  // Driver driver_10
  assign Src2 = decoder_3_out_2 ? x2_q : 32'bz;  // Driver driver_11
  assign Src2 = decoder_3_out_3 ? x3_q : 32'bz;  // Driver driver_12
  assign Src2 = decoder_3_out_4 ? x4_q : 32'bz;  // Driver driver_13
  assign Src2 = decoder_3_out_5 ? x5_q : 32'bz;  // Driver driver_14
  assign Src2 = decoder_3_out_6 ? x6_q : 32'bz;  // Driver driver_15
  assign Src2 = decoder_3_out_7 ? x7_q : 32'bz;  // Driver driver_16
  assign Src3 = decoder_4_out_0 ? x0_q : 32'bz;  // Driver driver_17
  Decoder #(.Selector_Bits(3)) decoder_4 (
    .sel(Rs3), .out_0(decoder_4_out_0), .out_1(decoder_4_out_1), .out_2(decoder_4_out_2),
    .out_3(decoder_4_out_3), .out_4(decoder_4_out_4), .out_5(decoder_4_out_5), .out_6(decoder_4_out_6),
    .out_7(decoder_4_out_7));
  assign Src3 = decoder_4_out_1 ? x1_q : 32'bz;  // Driver driver_18
  assign Src3 = decoder_4_out_2 ? x2_q : 32'bz;  // Driver driver_19
  assign Src3 = decoder_4_out_3 ? x3_q : 32'bz;  // Driver driver_20
  assign Src3 = decoder_4_out_4 ? x4_q : 32'bz;  // Driver driver_21
  assign Src3 = decoder_4_out_5 ? x5_q : 32'bz;  // Driver driver_22
  assign Src3 = decoder_4_out_6 ? x6_q : 32'bz;  // Driver driver_23
  assign Src3 = decoder_4_out_7 ? x7_q : 32'bz;  // Driver driver_24
endmodule
