// Digital circuit Reg_file_rv32i.dig as structural Verilog
module Reg_file_rv32i (
  input  W_reg,
  input  [4:0] Rs3,
  input  [4:0] Rs1,
  input  [4:0] Rs2,
  input  [31:0] Data,
  input  [4:0] Rd,
  output [31:0] TEST,
  output [31:0] Src1,
  output [31:0] Src2
);

  wire and_1_out, and_2_out, and_3_out, and_4_out, decoder_1_out_0, decoder_1_out_1, decoder_1_out_2,
       decoder_1_out_3;
  wire [31:0] reg_file_8x32_0_1_src1, reg_file_8x32_0_1_src2, reg_file_8x32_0_1_src3, reg_file_8x32_1_src1,
       reg_file_8x32_1_src2, reg_file_8x32_1_src3, reg_file_8x32_2_src1, reg_file_8x32_2_src2,
       reg_file_8x32_2_src3, reg_file_8x32_3_src1, reg_file_8x32_3_src2, reg_file_8x32_3_src3;

  Decoder #(.Selector_Bits(2)) decoder_1 (
    .sel(Rd[4:3]), .out_0(decoder_1_out_0), .out_1(decoder_1_out_1), .out_2(decoder_1_out_2),
    .out_3(decoder_1_out_3));
  and and_1 (and_1_out, W_reg, decoder_1_out_0);
  and and_2 (and_2_out, W_reg, decoder_1_out_1);
  and and_3 (and_3_out, decoder_1_out_2, W_reg);
  and and_4 (and_4_out, decoder_1_out_3, W_reg);
  Reg_file_8x32_0 reg_file_8x32_0_1 (
    .Rd(Rd[2:0]), .Data(Data), .W_reg(and_1_out), .Rs1(Rs1[2:0]), .Rs2(Rs2[2:0]), .Rs3(Rs3[2:0]),
    .Src1(reg_file_8x32_0_1_src1), .Src2(reg_file_8x32_0_1_src2), .Src3(reg_file_8x32_0_1_src3));
  Reg_file_8x32 reg_file_8x32_1 (
    .Rd(Rd[2:0]), .Data(Data), .W_reg(and_2_out), .Rs1(Rs1[2:0]), .Rs2(Rs2[2:0]), .Rs3(Rs3[2:0]),
    .Src1(reg_file_8x32_1_src1), .Src2(reg_file_8x32_1_src2), .Src3(reg_file_8x32_1_src3));
  Reg_file_8x32 reg_file_8x32_2 (
    .Rd(Rd[2:0]), .Data(Data), .W_reg(and_3_out), .Rs1(Rs1[2:0]), .Rs2(Rs2[2:0]), .Rs3(Rs3[2:0]),
    .Src1(reg_file_8x32_2_src1), .Src2(reg_file_8x32_2_src2), .Src3(reg_file_8x32_2_src3));
  Reg_file_8x32 reg_file_8x32_3 (
    .Rd(Rd[2:0]), .Data(Data), .W_reg(and_4_out), .Rs1(Rs1[2:0]), .Rs2(Rs2[2:0]), .Rs3(Rs3[2:0]),
    .Src1(reg_file_8x32_3_src1), .Src2(reg_file_8x32_3_src2), .Src3(reg_file_8x32_3_src3));
  Multiplexer #(.Selector_Bits(2), .Bits(32)) multiplexer_1 (
    .sel(Rs3[4:3]), .in_0(reg_file_8x32_0_1_src3), .in_1(reg_file_8x32_1_src3), .in_2(reg_file_8x32_2_src3),
    .in_3(reg_file_8x32_3_src3), .out(TEST));
  Multiplexer #(.Selector_Bits(2), .Bits(32)) multiplexer_2 (
    .sel(Rs1[4:3]), .in_0(reg_file_8x32_0_1_src1), .in_1(reg_file_8x32_1_src1), .in_2(reg_file_8x32_2_src1),
    .in_3(reg_file_8x32_3_src1), .out(Src1));
  Multiplexer #(.Selector_Bits(2), .Bits(32)) multiplexer_3 (
    .sel(Rs2[4:3]), .in_0(reg_file_8x32_0_1_src2), .in_1(reg_file_8x32_1_src2), .in_2(reg_file_8x32_2_src2),
    .in_3(reg_file_8x32_3_src2), .out(Src2));
endmodule
